// Logisim project Lab_2.circ as structural Verilog: 1 circuit, main circuit main
module main (
  input  x,
  input  y,
  input  z
);

  wire f_2_out, F_3_out, f_out, not_1_out, not_2_out, or_1_out, x__y_prime_out, x_prime_out,
       x_prime_y_prime_out, x_prime_y_prime_z_out, x_y_prime_out, xy_out, xy_prime_out, xy_prime_z_out,
       xyz_out, z_x_y_prime____prime_out;

  not not_1 (not_1_out, x);
  not not_2 (not_2_out, y);
  and xy_prime (xy_prime_out, x, not_2_out);
  and x_prime_y_prime (x_prime_y_prime_out, not_1_out, not_2_out);
  and xy (xy_out, x, y);
  or x_y_prime (x_y_prime_out, x, not_2_out);
  nand x_prime (x_prime_out, x, x);
  and xy_prime_z (xy_prime_z_out, xy_prime_out, z);
  and x_prime_y_prime_z (x_prime_y_prime_z_out, x_prime_y_prime_out, z);
  and xyz (xyz_out, xy_out, z);
  nand x__y_prime (x__y_prime_out, x_prime_out, y);
  or or_1 (or_1_out, xy_prime_z_out, x_prime_y_prime_z_out);
  nand z_x_y_prime____prime (z_x_y_prime____prime_out, x__y_prime_out, z);
  or f (f_out, or_1_out, xyz_out);
  and f_2 (f_2_out, x_y_prime_out, z);
  nand F_3 (F_3_out, z_x_y_prime____prime_out, z_x_y_prime____prime_out);
endmodule
