// Logisim project Lab_3.circ as structural Verilog: 1 circuit, main circuit main
module main (
  input  x,
  input  y,
  input  z,
  input  p
);

  wire Even_Parity_Checker_out, Even_Parity_Generator_2_out, Even_Parity_Generator_out, nand_1_out,
       nand_2_out, not_1_out, not_2_out, not_3_out, not_4_out, Odd_Parity_Checker_out, x_prime_y__prime_out,
       x_XOR_y_out, xor_1_out, xor_2_out, xor_3_out, xy_prime__prime_out;

  not not_1 (not_1_out, x);
  not not_2 (not_2_out, y);
  not not_3 (not_3_out, z);
  xor xor_1 (xor_1_out, x, y);
  xor xor_2 (xor_2_out, x, y);
  nand xy_prime__prime (xy_prime__prime_out, x, not_2_out);
  nand x_prime_y__prime (x_prime_y__prime_out, not_1_out, y);
  xor xor_3 (xor_3_out, xor_1_out, z);
  nand x_XOR_y (x_XOR_y_out, xy_prime__prime_out, x_prime_y__prime_out);
  not not_4 (not_4_out, x_XOR_y_out);
  nand nand_1 (nand_1_out, x_XOR_y_out, not_3_out);
  nand nand_2 (nand_2_out, z, not_4_out);
  xor Even_Parity_Checker (Even_Parity_Checker_out, xor_3_out, p);
  not Odd_Parity_Checker (Odd_Parity_Checker_out, Even_Parity_Checker_out);
  xor Even_Parity_Generator (Even_Parity_Generator_out, xor_2_out, z);
  nand Even_Parity_Generator_2 (Even_Parity_Generator_2_out, nand_1_out, nand_2_out);
endmodule
