// Logisim project project.circ as structural Verilog: 1 circuit, main circuit main
module main (
  input  in_1,
  input  in_2,
  input  in_3,
  input  in_4,
  input  in_5,
  input  in_6,
  input  in_7,
  input  in_8,
  input  in_9
);

  wire A_out, and_1_out, and_2_out, and_3_out, and_4_out, and_5_out, and_6_out, and_7_out, and_8_out, B_out,
       C_out, D_out, E_out, F_out, G_out, not_1_out, not_2_out, not_3_out, not_4_out, or_1_out, or_2_out,
       or_3_out, or_4_out, or_5_out, or_6_out, or_7_out, or_8_out, or_9_out, or_10_out, or_11_out, or_12_out,
       or_13_out, or_14_out, or_15_out, or_16_out, or_17_out, w_out, w_prime_x_out, w_prime_x_prime_out,
       w_prime_y_prime_z_prime_out, w_prime_y_z_out, w_prime_z_out, w_x_out, w_x_prime_z_prime_out, w_y_out,
       x_out, x_prime_y_out, x_prime_y_prime_out, x_prime_z_prime_out, x_y_prime_out, x_y_prime_z_out,
       x_z_prime_out, xor_1_out, xor_2_out, xor_3_out, xor_4_out, xz_out, y_out, y_prime_z_prime_out,
       y_z_out, y_z_prime_out, z_out;

  xor xor_1 (xor_1_out, in_9, in_4);
  and and_1 (and_1_out, in_4, in_9);
  or or_1 (or_1_out, and_1_out, and_5_out);
  xor xor_2 (xor_2_out, in_3, in_8);
  and and_2 (and_2_out, in_3, in_8);
  or or_2 (or_2_out, and_2_out, and_6_out);
  xor xor_3 (xor_3_out, in_2, in_7);
  and and_3 (and_3_out, in_2, in_7);
  or or_3 (or_3_out, and_3_out, and_7_out);
  xor xor_4 (xor_4_out, in_1, in_6);
  and and_4 (and_4_out, in_1, in_6);
  or or_4 (or_4_out, and_4_out, and_8_out);
  LED led_1 (.in(or_4_out));
  xor z (z_out, in_5, xor_1_out);
  and and_5 (and_5_out, in_5, xor_1_out);
  xor y (y_out, or_1_out, xor_2_out);
  and and_6 (and_6_out, or_1_out, xor_2_out);
  xor x (x_out, or_2_out, xor_3_out);
  and and_7 (and_7_out, xor_3_out, or_2_out);
  xor w (w_out, or_3_out, xor_4_out);
  and and_8 (and_8_out, xor_4_out, or_3_out);
  not not_1 (not_1_out, z_out);
  not not_2 (not_2_out, y_out);
  not not_3 (not_3_out, x_out);
  not not_4 (not_4_out, w_out);
  and xz (xz_out, x_out, z_out);
  and x_prime_z_prime (x_prime_z_prime_out, not_3_out, not_1_out);
  and y_z (y_z_out, z_out, y_out);
  and y_prime_z_prime (y_prime_z_prime_out, not_2_out, not_1_out);
  and x_y_prime (x_y_prime_out, x_out, not_2_out);
  and x_z_prime (x_z_prime_out, not_1_out, x_out);
  and w_prime_x_prime (w_prime_x_prime_out, not_3_out, not_4_out);
  and x_prime_y_prime (x_prime_y_prime_out, not_2_out, not_3_out);
  and w_prime_y_prime_z_prime (w_prime_y_prime_z_prime_out, y_prime_z_prime_out, not_4_out);
  and w_prime_y_z (w_prime_y_z_out, y_z_out, not_4_out);
  and x_prime_y (x_prime_y_out, y_out, not_3_out);
  and w_x (w_x_out, x_out, w_out);
  and y_z_prime (y_z_prime_out, not_1_out, y_out);
  and w_y (w_y_out, y_out, w_out);
  and w_prime_x (w_prime_x_out, x_out, not_4_out);
  and w_prime_z (w_prime_z_out, z_out, not_4_out);
  and x_y_prime_z (x_y_prime_z_out, x_y_prime_out, z_out);
  or C (C_out, w_prime_y_z_out, or_5_out);
  or or_5 (or_5_out, w_prime_y_prime_z_prime_out, or_6_out);
  or or_6 (or_6_out, x_prime_y_prime_out, w_prime_x_prime_out);
  or B (B_out, x_z_prime_out, or_7_out);
  or or_7 (or_7_out, x_y_prime_out, or_8_out);
  or or_8 (or_8_out, y_prime_z_prime_out, w_out);
  or A (A_out, y_z_out, or_9_out);
  or or_9 (or_9_out, xz_out, w_x_prime_z_prime_out);
  or w_x_prime_z_prime (w_x_prime_z_prime_out, x_prime_z_prime_out, w_out);
  or G (G_out, x_y_prime_z_out, or_10_out);
  or or_10 (or_10_out, w_x_out, or_11_out);
  or or_11 (or_11_out, y_z_prime_out, or_12_out);
  or or_12 (or_12_out, x_prime_y_out, x_prime_z_prime_out);
  or F (F_out, w_prime_z_out, or_13_out);
  or or_13 (or_13_out, w_prime_x_out, x_prime_y_prime_out);
  or E (E_out, w_y_out, or_14_out);
  or or_14 (or_14_out, y_z_prime_out, or_15_out);
  or or_15 (or_15_out, w_x_out, x_prime_z_prime_out);
  or D (D_out, x_prime_y_out, or_16_out);
  or or_16 (or_16_out, x_z_prime_out, or_17_out);
  or or_17 (or_17_out, x_y_prime_out, w_out);
  _7_Segment_Display u_7_segment_display_1 (
    .g(D_out), .f(B_out), .a(A_out), .b(C_out), .e(E_out), .d(G_out), .c(F_out));  // open: dp
endmodule
